# Fritzing sketch BinaryDice (saved by Fritzing 0.7.12b)
breadboards: 1

parts:
  Arduino1 = Arduino
  LED_BIT0 = LED - 5mm [color="Green (555nm)" package="5 mm [THT]"]
  LED_BIT1 = LED - 5mm [color="Yellow (595nm)" package="5 mm [THT]"]
  LED_BIT2 = LED - 5mm [color="Red (633nm)" package="5 mm [THT]"]
  R2_1K = Resistor [tolerance=±5% resistance=1k package=THT]
  START_BUTTON_PIN = Pushbutton [package="[THT]"]
  GUESS_BUTTON_PIN = Pushbutton [package="[THT]"]
  R4_10K = Resistor [tolerance=±5% resistance=10k package=THT]
  R5_10K = Resistor [tolerance=±5% resistance=10k package=THT]
  R3_1K = Resistor [tolerance=±5% resistance=1k package=THT]
  R1_1K = Resistor [tolerance=±5% resistance=1k package=THT]

nets:
  N1: Arduino1.GND, LED_BIT0.cathode, LED_BIT1.cathode, LED_BIT2.cathode, R4_10K.Pin_1, R5_10K.Pin_1
  N2: Arduino1.D12, R3_1K.Pin_1
  N3: Arduino1.D11, R2_1K.Pin_1
  N4: Arduino1.D10, R1_1K.Pin_1
  N5: Arduino1.D7, GUESS_BUTTON_PIN.Pin_1, GUESS_BUTTON_PIN.Pin_2, R4_10K.Pin_0
  N6: Arduino1.D5, START_BUTTON_PIN.Pin_1, START_BUTTON_PIN.Pin_2, R5_10K.Pin_0
  N7: Arduino1.3V3, START_BUTTON_PIN.Pin_3, START_BUTTON_PIN.Pin_4, GUESS_BUTTON_PIN.Pin_3, GUESS_BUTTON_PIN.Pin_4
  N8: LED_BIT0.anode, R3_1K.Pin_0
  N9: LED_BIT1.anode, R2_1K.Pin_0
  N10: LED_BIT2.anode, R1_1K.Pin_0
